# Fritzing sketch MazeUnlockReceiverScheme (saved by Fritzing 0.9.3b)
breadboards: 1

parts:
  Součástka2 = 24 NeoPixel Ring [part_number=1586]
  Součástka4 = Arduino Nano (Rev3.0)
  Součástka5 = NRF24L01+ Breakout Board

nets:
  N1: Součástka2.IN, Součástka4.D5
  VDD: Součástka2.VDD, Součástka4.5V
  GND: Součástka2.GND, Součástka4.GND, Součástka5.GND
  N2: Součástka4.D8, Součástka5.CS
  N3: Součástka4.D9, Součástka5.CE
  N4: Součástka4.D11/MOSI, Součástka5.MOSI
  N5: Součástka4.D12/MISO, Součástka5.MISO
  3V3: Součástka4.3V3, Součástka5.VCC
  N6: Součástka4.D13/SCK, Součástka5.SCK

custom parts:
  24 NeoPixel Ring: 24 ultra bright smart LED NeoPixels are arranged in a circle with 2.6" (66mm) outer diameter. The rings are 'chainable' - connect the output pin of one to the input pin of another. Use only one microcontroller pin to control as many as you can chain together! Each LED is addressable as the driver chip is inside the LED. Each one has ~18mA constant current drive so the color will be very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
