# Fritzing sketch MazeUnlockTransmitterScheme (saved by Fritzing 0.9.3b)
breadboards: 1

parts:
  Součástka1 = Arduino Nano (Rev3.0)
  Součástka2 = Thumb Joystick
  Součástka3 = NRF24L01+ Breakout Board
  SW2 = DIP SWITCH [package=dipswitch-02]

nets:
  GND: Součástka1.GND, Součástka2.GND, Součástka3.GND, SW2.1
  N1: Součástka1.D3, Součástka2.SEL
  N2: Součástka1.D7, SW2.4
  N3: Součástka1.D8, Součástka3.CS
  N4: Součástka1.D9, Součástka3.CE
  N5: Součástka1.D11/MOSI, Součástka3.MOSI
  N6: Součástka1.D12/MISO, Součástka3.MISO
  5V: Součástka1.5V, Součástka2.VCC
  N7: Součástka1.A6, Součástka2.HORZ
  N8: Součástka1.A5, Součástka2.VERT
  3V3: Součástka1.3V3, Součástka3.VCC
  N9: Součástka1.D13/SCK, Součástka3.SCK
